// Logisim project Circuitos Lógicos.circ as structural Verilog: 1 circuit, main circuit main
module main (
  input  A,
  input  B,
  input  C,
  input  D,
  input  A_2,
  input  B_2,
  input  C_2,
  input  D_2,
  output out_9,
  output out_10
);

  wire and_1_out, and_2_out, and_3_out, and_4_out, and_5_out, not_1_out, not_2_out, or_1_out, or_2_out,
       or_3_out;

  and and_1 (and_1_out, A, B);
  or or_1 (or_1_out, B, D);
  or or_2 (or_2_out, A_2, D_2);
  and and_2 (and_2_out, C_2, B_2);
  not not_1 (not_1_out, and_1_out);
  not not_2 (not_2_out, or_1_out);
  and and_3 (and_3_out, or_2_out, B_2);
  and and_4 (and_4_out, not_1_out, C);
  and and_5 (and_5_out, A, not_2_out);
  or or_3 (or_3_out, A_2, and_3_out, and_2_out);
  not not_3 (out_10, or_3_out);
  or or_4 (out_9, and_4_out, and_5_out);

  // Notes on the sheet:
  //   Exercício a)
  //   Exercício b)
endmodule
